# Fritzing sketch SoftLED-01 (saved by Fritzing 0.9.3b)

parts:
  Part1 = Arduino Nano (Rev3.0)
  R1 = Resistor [tolerance=±5% resistance=10k package=THT]
  S1 = Toggle Switch [package=THT]
  R3 = Resistor [tolerance=±5% resistance=1k package=THT]
  LED1 = LED - 5mm [color="Yellow (595nm)" package="5 mm [THT]"]
  LED2 = LED - 5mm [color="Red (633nm)" package="5 mm [THT]"]
  R2 = Resistor [tolerance=±5% resistance=1k package=THT]

nets:
  GND: Part1.GND, S1.L2
  N1: Part1.D2, R1.Pin_0, S1.COM
  5V: Part1.5V, R1.Pin_1, LED1.anode, LED2.anode
  N2: R3.Pin_1, LED2.cathode
  N3: LED1.cathode, R2.Pin_1
